// Digital circuit Ugur Oztunc.dig as structural Verilog
module Ugur_Oztunc (
  input  Bit_1,
  input  Bit_2,
  input  Bit_3
);

  wire and_1_out, and_2_out, and_3_out, and_4_out, and_5_out, and_6_out, and_7_out, and_8_out, and_9_out,
       and_10_out, and_11_out, and_12_out, and_13_out, and_14_out, and_15_out, and_16_out, not_1_out,
       not_2_out, not_3_out, or_1_out, or_2_out, or_3_out, or_4_out, or_5_out, or_6_out, or_7_out;

  not not_1 (not_1_out, Bit_3);
  not not_2 (not_2_out, Bit_2);
  not not_3 (not_3_out, Bit_1);
  and and_1 (and_1_out, not_3_out, not_1_out);
  and and_2 (and_2_out, not_3_out, Bit_2);
  and and_3 (and_3_out, Bit_1, not_2_out, Bit_3);
  and and_4 (and_4_out, Bit_2, not_1_out);
  or or_1 (or_1_out, Bit_1, not_2_out, Bit_3);
  and and_5 (and_5_out, not_3_out, not_2_out);
  and and_6 (and_6_out, Bit_1, Bit_2);
  and and_7 (and_7_out, not_3_out, not_1_out);
  and and_8 (and_8_out, Bit_1, Bit_3);
  and and_9 (and_9_out, not_3_out, not_1_out);
  and and_10 (and_10_out, not_3_out, Bit_2);
  and and_11 (and_11_out, not_3_out, not_2_out);
  and and_12 (and_12_out, not_3_out, Bit_3);
  and and_13 (and_13_out, not_2_out, Bit_3);
  and and_14 (and_14_out, not_3_out, Bit_3);
  and and_15 (and_15_out, not_2_out, Bit_3);
  and and_16 (and_16_out, Bit_2, not_1_out);
  or or_2 (or_2_out, and_1_out, and_2_out, and_3_out, and_4_out);
  or or_3 (or_3_out, and_5_out, and_6_out, not_1_out);
  or or_4 (or_4_out, and_7_out, and_8_out, Bit_2);
  or or_5 (or_5_out, and_9_out, and_10_out);
  or or_6 (or_6_out, and_11_out, and_12_out, and_13_out);
  or or_7 (or_7_out, and_14_out, and_15_out, and_16_out);
  Seven_Seg seven_seg_1 (
    .a(or_4_out), .b(or_3_out), .c(or_1_out), .d(or_2_out), .e(or_5_out), .f(or_6_out), .g(or_7_out),
    .dp(1'b0));
endmodule
