// Digital circuit shifter.dig as structural Verilog
module shifter (
  input  [3:0] IN,
  input  EN,
  input  DA,
  input  CLK,
  input  RST,
  output [3:0] ID1,
  output [3:0] ID0,
  output [6:0] HEX
);

  wire and_1_out;
  wire [3:0] multiplexer_1_out, multiplexer_2_out;
  wire [6:0] mul_1_mul;
  wire [7:7] mul_1_mul_2;

  and and_1 (and_1_out, EN, DA);
  Multiplexer #(.Bits(4)) multiplexer_1 (.sel(and_1_out), .in_0(ID0), .in_1(IN), .out(multiplexer_1_out));
  Multiplexer #(.Bits(4)) multiplexer_2 (.sel(and_1_out), .in_0(ID1), .in_1(ID0), .out(multiplexer_2_out));
  D_FF_AS #(.Bits(4)) ID_0 (.Set(1'b0), .D(multiplexer_1_out), .C(CLK), .Clr(~RST), .Q(ID0));  // open: nQ
  D_FF_AS #(.Bits(4)) ID_1 (.Set(1'b0), .D(multiplexer_2_out), .C(CLK), .Clr(~RST), .Q(ID1));  // open: nQ
  Mul #(.Bits(4)) mul_1 (.a(4'b1010), .b(ID1), .mul({mul_1_mul_2[7], mul_1_mul}));
  Add #(.Bits(7)) add_1 (.a(mul_1_mul), .b({3'b000, ID0}), .c_i(1'b0), .s(HEX));  // open: c_o
endmodule
