// Digital circuit shifter_pwd.dig as structural Verilog
module shifter_pwd (
  input  [3:0] DATA_in,
  input  [15:0] PWD_in,
  input  EN,
  input  DA,
  input  CLK,
  input  RST,
  output MATCH,
  output LED1,
  output LED2,
  output LED3,
  output LED4
);

  wire and_1_out, and_2_out, and_3_out, and_4_out, and_5_out, comparator_1_eq;
  wire [4:0] multiplexer_1_out, multiplexer_2_out, multiplexer_3_out, multiplexer_4_out;
  wire [4:1] P_0_q, P_1_q, P_2_q, P_3_q;

  and and_1 (and_1_out, EN, RST);
  Multiplexer #(.Bits(5)) multiplexer_1 (
    .sel(and_2_out), .in_0({P_0_q, LED1}), .in_1({DATA_in, EN}), .out(multiplexer_1_out));
  and and_2 (and_2_out, DA, ~LED1);  // And
  Multiplexer #(.Bits(5)) multiplexer_2 (
    .sel(and_3_out), .in_0({P_1_q, LED2}), .in_1({DATA_in, EN}), .out(multiplexer_2_out));
  and and_3 (and_3_out, DA, ~LED2, LED1);  // And
  Multiplexer #(.Bits(5)) multiplexer_3 (
    .sel(and_4_out), .in_0({P_2_q, LED3}), .in_1({DATA_in, EN}), .out(multiplexer_3_out));
  and and_4 (and_4_out, DA, ~LED3, LED2);  // And
  Multiplexer #(.Bits(5)) multiplexer_4 (
    .sel(and_5_out), .in_0({P_3_q, LED4}), .in_1({DATA_in, EN}), .out(multiplexer_4_out));
  and and_5 (and_5_out, DA, ~LED4, LED3);  // And
  D_FF_AS #(.Bits(5)) P_0 (
    .Set(1'b0), .D(multiplexer_1_out), .C(CLK), .Clr(~and_1_out), .Q({P_0_q, LED1}));  // open: nQ
  D_FF_AS #(.Bits(5)) P_1 (
    .Set(1'b0), .D(multiplexer_2_out), .C(CLK), .Clr(~and_1_out), .Q({P_1_q, LED2}));  // open: nQ
  D_FF_AS #(.Bits(5)) P_2 (
    .Set(1'b0), .D(multiplexer_3_out), .C(CLK), .Clr(~and_1_out), .Q({P_2_q, LED3}));  // open: nQ
  D_FF_AS #(.Bits(5)) P_3 (
    .Set(1'b0), .D(multiplexer_4_out), .C(CLK), .Clr(~and_1_out), .Q({P_3_q, LED4}));  // open: nQ
  Comparator #(.Bits(16)) comparator_1 (
    .a({P_0_q, P_1_q, P_2_q, P_3_q}), .b(PWD_in), .eq(comparator_1_eq));  // open: gt, lt
  and and_6 (MATCH, LED4, comparator_1_eq);
endmodule
