// Digital circuit timer.dig as structural Verilog
module timer (
  input  START,
  input  CLK,
  input  RST,
  output RESET,
  output DIS
);

  wire and_1_out, and_3_out, and_4_out, d_ff_1_nq, d_ff_2_nq, d_ff_3_nq, d_ff_4_nq, d_ff_5_nq, d_ff_5_q,
       d_ff_as_1_nq, d_ff_as_1_q, d_ff_as_2_nq, d_ff_as_2_q, d_ff_as_3_nq, d_ff_as_3_q, d_ff_as_4_nq,
       d_ff_as_4_q, multiplexer_1_out, multiplexer_2_out, multiplexer_3_out;

  D_FF d_ff_1 (.D(d_ff_1_nq), .C(d_ff_3_nq), .nQ(d_ff_1_nq));  // open: Q
  D_FF d_ff_2 (.D(d_ff_2_nq), .C(d_ff_4_nq), .nQ(d_ff_2_nq));  // open: Q
  D_FF d_ff_3 (.D(d_ff_3_nq), .C(CLK), .nQ(d_ff_3_nq));  // open: Q
  D_FF d_ff_4 (.D(d_ff_4_nq), .C(d_ff_1_nq), .nQ(d_ff_4_nq));  // open: Q
  D_FF d_ff_5 (.D(d_ff_5_nq), .C(d_ff_2_nq), .Q(d_ff_5_q), .nQ(d_ff_5_nq));
  and and_1 (and_1_out, ~RESET, START, RST);  // And
  D_FF_AS d_ff_as_1 (.Set(1'b0), .D(d_ff_as_1_nq), .C(d_ff_5_q), .Clr(~and_1_out), .Q(d_ff_as_1_q), .nQ(d_ff_as_1_nq));
  D_FF_AS d_ff_as_2 (
    .Set(1'b0), .D(multiplexer_1_out), .C(d_ff_5_q), .Clr(~and_1_out), .Q(d_ff_as_2_q), .nQ(d_ff_as_2_nq));
  D_FF_AS d_ff_as_3 (
    .Set(1'b0), .D(multiplexer_2_out), .C(d_ff_5_q), .Clr(~and_1_out), .Q(d_ff_as_3_q), .nQ(d_ff_as_3_nq));
  D_FF_AS d_ff_as_4 (
    .Set(1'b0), .D(multiplexer_3_out), .C(d_ff_5_q), .Clr(~and_1_out), .Q(d_ff_as_4_q), .nQ(d_ff_as_4_nq));
  Multiplexer multiplexer_1 (.sel(d_ff_as_1_q), .in_0(d_ff_as_2_q), .in_1(d_ff_as_2_nq), .out(multiplexer_1_out));
  Multiplexer multiplexer_2 (.sel(and_3_out), .in_0(d_ff_as_3_q), .in_1(d_ff_as_3_nq), .out(multiplexer_2_out));
  Multiplexer multiplexer_3 (.sel(and_4_out), .in_0(d_ff_as_4_q), .in_1(d_ff_as_4_nq), .out(multiplexer_3_out));
  and and_2 (RESET, d_ff_as_1_q, ~d_ff_as_2_q, ~d_ff_as_3_q, d_ff_as_4_q);  // And
  and and_3 (and_3_out, d_ff_as_1_q, d_ff_as_2_q);
  and and_4 (and_4_out, d_ff_as_3_q, and_3_out);

  assign DIS = START;
endmodule
