// Digital circuit mul2bit.dig as structural Verilog
module mul2bit (
  input  in_1,
  input  in_2,
  input  in_3,
  input  in_4
);

  wire [3:0] core_1_m;

  Seven_Seg_Hex seven_seg_hex_1 (.d({2'b00, in_1, in_2}), .dp(1'b0));
  Seven_Seg_Hex seven_seg_hex_2 (.d({2'b00, in_3, in_4}), .dp(1'b0));
  core core_1 (.A0(in_2), .A1(in_1), .B0(in_4), .B1(in_3), .M(core_1_m));
  Seven_Seg_Hex seven_seg_hex_3 (.d(core_1_m), .dp(1'b0));

  // Notes on the sheet:
  //   x
  //   =
endmodule
