// Digital circuit Simplified 7 Seg Decoder 3 Bit.dig as structural Verilog
module Simplified_7_Seg_Decoder_3_Bit (
  input  _1st_Bit,
  input  _2nd_Bit,
  input  _3rd_Bit,
  output D,
  output C,
  output B,
  output A,
  output E,
  output F,
  output G
);

  wire and_1_out, and_2_out, and_3_out, and_4_out, and_5_out, and_6_out, and_7_out, and_8_out, and_9_out,
       and_10_out, and_11_out, and_12_out, and_13_out, and_14_out, and_15_out, and_16_out, not_1_out,
       not_2_out, not_3_out;

  not not_1 (not_1_out, _3rd_Bit);
  not not_2 (not_2_out, _2nd_Bit);
  not not_3 (not_3_out, _1st_Bit);
  and and_1 (and_1_out, not_3_out, not_1_out);
  or or_1 (D, and_1_out, and_2_out, and_3_out, and_4_out);
  and and_2 (and_2_out, not_3_out, _2nd_Bit);
  and and_3 (and_3_out, _1st_Bit, not_2_out, _3rd_Bit);
  and and_4 (and_4_out, _2nd_Bit, not_1_out);
  or or_2 (C, _1st_Bit, not_2_out, _3rd_Bit);
  and and_5 (and_5_out, not_3_out, not_2_out);
  or or_3 (B, and_5_out, and_6_out, not_1_out);
  and and_6 (and_6_out, _1st_Bit, _2nd_Bit);
  and and_7 (and_7_out, not_3_out, not_1_out);
  or or_4 (A, and_7_out, and_8_out, _2nd_Bit);
  and and_8 (and_8_out, _1st_Bit, _3rd_Bit);
  or or_5 (E, and_9_out, and_10_out);
  and and_9 (and_9_out, not_3_out, not_1_out);
  and and_10 (and_10_out, not_3_out, _2nd_Bit);
  and and_11 (and_11_out, not_3_out, not_2_out);
  or or_6 (F, and_11_out, and_12_out, and_13_out);
  and and_12 (and_12_out, not_3_out, _3rd_Bit);
  and and_13 (and_13_out, not_2_out, _3rd_Bit);
  and and_14 (and_14_out, not_3_out, _3rd_Bit);
  or or_7 (G, and_14_out, and_15_out, and_16_out);
  and and_15 (and_15_out, not_2_out, _3rd_Bit);
  and and_16 (and_16_out, _2nd_Bit, not_1_out);
endmodule
