// Digital circuit part1.dig as structural Verilog
module part1 (
  input  S2,
  input  S1,
  input  S0,
  output D0,
  output D1,
  output D2,
  output D3,
  output D4,
  output D5,
  output D6,
  output D7
);

  wire not_1_out;

  not not_1 (not_1_out, S2);
  Demultiplexer #(.Selector_Bits(2)) demultiplexer_1 (
    .sel({S1, S0}), .in(not_1_out), .out_0(D0), .out_1(D1), .out_2(D2), .out_3(D3));
  Demultiplexer #(.Selector_Bits(2)) demultiplexer_2 (
    .sel({S1, S0}), .in(S2), .out_0(D4), .out_1(D5), .out_2(D6), .out_3(D7));
endmodule
