// Digital circuit part2.dig as structural Verilog
module part2 (
  input  A,
  input  B,
  input  C,
  input  D,
  input  E,
  input  F,
  input  G,
  input  H,
  input  S0,
  input  S1,
  input  S2,
  output Out
);

  wire multiplexer_1_out, multiplexer_2_out, multiplexer_3_out, multiplexer_4_out, multiplexer_5_out,
       multiplexer_6_out;

  Multiplexer multiplexer_1 (.sel(S0), .in_0(A), .in_1(B), .out(multiplexer_1_out));
  Multiplexer multiplexer_2 (.sel(S0), .in_0(C), .in_1(D), .out(multiplexer_2_out));
  Multiplexer multiplexer_3 (.sel(S0), .in_0(E), .in_1(F), .out(multiplexer_3_out));
  Multiplexer multiplexer_4 (.sel(S0), .in_0(G), .in_1(H), .out(multiplexer_4_out));
  Multiplexer multiplexer_5 (.sel(S1), .in_0(multiplexer_1_out), .in_1(multiplexer_2_out), .out(multiplexer_5_out));
  Multiplexer multiplexer_6 (.sel(S1), .in_0(multiplexer_3_out), .in_1(multiplexer_4_out), .out(multiplexer_6_out));
  Multiplexer multiplexer_7 (.sel(S2), .in_0(multiplexer_5_out), .in_1(multiplexer_6_out), .out(Out));
endmodule
