// Digital circuit part3.dig as structural Verilog
module part3 (
  input  x,
  input  y,
  input  z,
  output F_x_y_z
);

  wire decoder_1_out_2, decoder_1_out_3, decoder_1_out_6, or_1_out;

  Decoder #(.Selector_Bits(3)) decoder_1 (
    .sel({z, y, x}), .out_2(decoder_1_out_2), .out_3(decoder_1_out_3), .out_6(decoder_1_out_6));  // open: out_0, out_1, out_4, out_5, out_7
  or or_1 (or_1_out, decoder_1_out_2, decoder_1_out_3);
  nor nor_1 (F_x_y_z, or_1_out, decoder_1_out_6);
endmodule
