// Digital circuit part4.dig as structural Verilog
module part4 (
  input  A,
  input  B,
  input  C_in,
  output S,
  output C_out
);

  wire not_1_out, not_2_out;

  not not_1 (not_1_out, C_in);
  Multiplexer #(.Selector_Bits(2)) multiplexer_1 (
    .sel({B, A}), .in_0(C_in), .in_1(not_1_out), .in_2(not_1_out), .in_3(C_in), .out(S));
  Multiplexer #(.Selector_Bits(2)) multiplexer_2 (
    .sel({B, A}), .in_0(1'b0), .in_1(C_in), .in_2(C_in), .in_3(not_2_out), .out(C_out));
  not not_2 (not_2_out, 1'b0);
endmodule
