// Digital circuit rotarytest.dig as structural Verilog
module rotarytest (
  input  clk
);

  wire rotencoder_1_p1, rotencoder_1_p2, statemachine_1_out;
  wire [3:0] upcounter_1_cnt;

  // RotEncoder rotencoder_1: pin names not known; wires that end beside it: rotencoder_1_p1, rotencoder_1_p2
  statemachine statemachine_1 (.A(rotencoder_1_p1), .B(rotencoder_1_p2), .CLK(clk), .OUT(statemachine_1_out));
  upcounter upcounter_1 (.EN(statemachine_1_out), .LOAD(1'b0), .IN(4'b0000), .CLK(clk), .CNT(upcounter_1_cnt));
  Seven_Seg_Hex seven_seg_hex_1 (.d(upcounter_1_cnt), .dp(1'b0));

  // Notes on the sheet:
  //   clk: Hz: 20
  //   A
  //   B
endmodule
