// Digital circuit statemachine.dig as structural Verilog
module statemachine (
  input  A,
  input  B,
  input  CLK,
  output OUT
);

  wire and_1_out, and_2_out, and_3_out, and_4_out, and_5_out, not_1_out, not_2_out, or_1_out, or_2_out,
       S_0_nq, S_0_q, S_1_nq, S_1_q;

  not not_1 (not_1_out, A);
  not not_2 (not_2_out, B);
  and and_1 (and_1_out, not_1_out, B, S_1_nq);
  and and_2 (and_2_out, A, not_2_out, S_1_q);
  and and_3 (and_3_out, S_1_nq, S_0_q, A, B);
  and and_4 (and_4_out, S_1_q, A, not_2_out);
  and and_5 (and_5_out, S_1_q, A, S_0_nq);
  or or_1 (or_1_out, and_1_out, and_2_out);
  or or_2 (or_2_out, and_3_out, and_4_out, and_5_out);
  D_FF S_0 (.D(or_1_out), .C(CLK), .Q(S_0_q), .nQ(S_0_nq));
  D_FF S_1 (.D(or_2_out), .C(CLK), .Q(S_1_q), .nQ(S_1_nq));
  and and_6 (OUT, S_0_q, not_1_out, not_2_out, S_1_q);
endmodule
