// Digital circuit mode_selector.dig as structural Verilog
module mode_selector (
  input  ID,
  input  PWD,
  input  DIS,
  input  RESET,
  input  CLK,
  input  RST,
  output IDO,
  output PWDO
);

  wire and_1_out, and_2_out, or_1_out;

  and and_1 (and_1_out, PWDO, ~ID);  // And
  and and_2 (and_2_out, ~RESET, RST);  // And
  or or_1 (or_1_out, and_1_out, PWD, DIS);
  D_FF_AS d_ff_as_1 (.Set(1'b0), .D(or_1_out), .C(CLK), .Clr(~and_2_out), .Q(PWDO), .nQ(IDO));
endmodule
